# Fritzing sketch esp32-vl53l0x-sensor-circuit-diagram (saved by Fritzing 0.9.4)
breadboards: 1

parts:
  U1 = Wemos Lolin D32

nets:
  N1: U1.pin_22, U1.pin_37

custom parts:
  Wemos Lolin D32: Based on Peter Van Epp (vanepp in forums) Wemos Lolin 32 wifi and blue tooth board based on the ESP-32 cpu
